# Fritzing sketch IRLKTANEfritzing (saved by Fritzing 0.9.4)
breadboards: 14

parts:
  LCD4 = LCD screen
  LCM1602_IIC2 = LCM1602 IIC [part_number="LCM1602 IIC" chip_label="LCM1602 IIC" package="DIP (Dual Inline) [THT]"]
  Part8 = TM1637
  LCD5 = LCD screen
  LED31 = LED - 5mm [color="Red (633nm)" package="5 mm [THT]"]
  LED32 = LED - 5mm [color="Green (560nm)" package="5 mm [THT]"]
  LED33 = LED - 5mm [color="Yellow (585nm)" package="5 mm [THT]"]
  LED34 = LED - 5mm [color="Blue (470nm)" package="5 mm [THT]"]
  LED35 = LED - 5mm [color="Green (560nm)" package="5 mm [THT]"]
  LED36 = LED - 5mm [color="Green (560nm)" package="5 mm [THT]"]
  LED37 = LED - 5mm [color="Green (560nm)" package="5 mm [THT]"]
  LED38 = LED - 5mm [color="Green (560nm)" package="5 mm [THT]"]
  LED39 = LED - 5mm [color="Green (560nm)" package="5 mm [THT]"]
  LED40 = LED - 5mm [color="Green (560nm)" package="5 mm [THT]"]
  LED41 = LED - 5mm [color="Green (560nm)" package="5 mm [THT]"]
  LED42 = LED - 5mm [color="Green (560nm)" package="5 mm [THT]"]
  LED43 = LED - 5mm [color="Green (560nm)" package="5 mm [THT]"]
  LED44 = LED - 5mm [color="Green (560nm)" package="5 mm [THT]"]
  LED45 = LED - 5mm [color="Green (560nm)" package="5 mm [THT]"]
  LED46 = LED - 5mm [color="Green (560nm)" package="5 mm [THT]"]
  Part9 = Arduino Mega 2560 (Rev3)
  R1 = Resistor [tolerance=±5% resistance=330 package="0603 [SMD]"]
  R2 = Resistor [tolerance=±5% resistance=330 package="0603 [SMD]"]
  R3 = Resistor [tolerance=±5% resistance=330 package="0603 [SMD]"]
  R4 = Resistor [tolerance=±5% resistance=330 package="0603 [SMD]"]
  R5 = Resistor [tolerance=±5% resistance=330 package="0603 [SMD]"]
  R6 = Resistor [tolerance=±5% resistance=330 package="0603 [SMD]"]
  R7 = Resistor [tolerance=±5% resistance=330 package="0603 [SMD]"]
  R8 = Resistor [tolerance=±5% resistance=330 package="0603 [SMD]"]
  R9 = Resistor [tolerance=±5% resistance=330 package="0603 [SMD]"]
  R10 = Resistor [tolerance=±5% resistance=330 package="0603 [SMD]"]
  R11 = Resistor [tolerance=±5% resistance=330 package="0603 [SMD]"]
  R12 = Resistor [tolerance=±5% resistance=330 package="0603 [SMD]"]
  LED47 = LED - 5mm [color="Green (560nm)" package="5 mm [THT]"]
  R13 = Resistor [tolerance=±5% resistance=330 package="0603 [SMD]"]
  R14 = Resistor [tolerance=±5% resistance=330 package="0603 [SMD]"]
  R15 = Resistor [tolerance=±5% resistance=220 package="0603 [SMD]"]
  R16 = Resistor [tolerance=±5% resistance=100 package="0603 [SMD]"]
  R17 = Resistor [tolerance=±5% resistance=220 package="0603 [SMD]"]
  S11 = Pushbutton [package="[THT]"]
  S12 = Pushbutton [package="[THT]"]
  S13 = Pushbutton [package="[THT]"]
  S14 = Pushbutton [package="[THT]"]
  R18 = Resistor [tolerance=±5% resistance=10k package="0603 [SMD]"]
  R19 = Resistor [tolerance=±5% resistance=10k package="0603 [SMD]"]
  R20 = Resistor [tolerance=±5% resistance=10k package="0603 [SMD]"]
  R21 = Resistor [tolerance=±5% resistance=10k package="0603 [SMD]"]
  R22 = Resistor [tolerance=±5% resistance=10k package="0603 [SMD]"]
  S15 = Pushbutton [package="[THT]"]
  S16 = Pushbutton [package="[THT]"]
  S17 = Pushbutton [package="[THT]"]
  S18 = Pushbutton [package="[THT]"]
  S19 = Pushbutton [package="[THT]"]
  S20 = Pushbutton [package="[THT]"]
  R23 = Resistor [tolerance=±5% resistance=10k package="0603 [SMD]"]
  R24 = Resistor [tolerance=±5% resistance=10k package="0603 [SMD]"]
  R25 = Resistor [tolerance=±5% resistance=10k package="0603 [SMD]"]
  R26 = Resistor [tolerance=±5% resistance=10k package="0603 [SMD]"]
  R27 = Resistor [tolerance=±5% resistance=10k package="0603 [SMD]"]
  LED48 = LED - 5mm [color="Green (560nm)" package="5 mm [THT]"]
  LED49 = LED - 5mm [color="Green (560nm)" package="5 mm [THT]"]
  LED50 = LED - 5mm [color="Green (560nm)" package="5 mm [THT]"]
  R28 = Resistor [tolerance=±5% resistance=330 package="0603 [SMD]"]
  R29 = Resistor [tolerance=±5% resistance=330 package="0603 [SMD]"]
  R30 = Resistor [tolerance=±5% resistance=330 package="0603 [SMD]"]
  R31 = Resistor [tolerance=±5% resistance=330 package="0603 [SMD]"]
  LED51 = LED - 5mm [color="Green (560nm)" package="5 mm [THT]"]
  LCD6 = LCD screen  # not connected
  S21 = Pushbutton [package="[THT]"]
  S22 = Pushbutton [package="[THT]"]
  R32 = Resistor [tolerance=±5% resistance=10k package="0603 [SMD]"]
  R33 = Resistor [tolerance=±5% resistance=10k package="0603 [SMD]"]
  S23 = Pushbutton [package="[THT]"]
  S24 = Pushbutton [package="[THT]"]
  S25 = Pushbutton [package="[THT]"]
  S26 = Pushbutton [package="[THT]"]
  S27 = Pushbutton [package="[THT]"]
  S28 = Pushbutton [package="[THT]"]
  S29 = Pushbutton [package="[THT]"]
  S30 = Pushbutton [package="[THT]"]
  S31 = Pushbutton [package="[THT]"]
  S32 = Pushbutton [package="[THT]"]
  R34 = Resistor [tolerance=±5% resistance=10k package="0603 [SMD]"]
  R35 = Resistor [tolerance=±5% resistance=10k package="0603 [SMD]"]
  R36 = Resistor [tolerance=±5% resistance=10k package="0603 [SMD]"]
  R37 = Resistor [tolerance=±5% resistance=10k package="0603 [SMD]"]
  R38 = Resistor [tolerance=±5% resistance=10k package="0603 [SMD]"]
  R39 = Resistor [tolerance=±5% resistance=10k package="0603 [SMD]"]
  R40 = Resistor [tolerance=±5% resistance=10k package="0603 [SMD]"]
  R41 = Resistor [tolerance=±5% resistance=10k package="0603 [SMD]"]
  R42 = Resistor [tolerance=±5% resistance=10k package="0603 [SMD]"]
  R43 = Resistor [tolerance=±5% resistance=10k package="0603 [SMD]"]
  LED52 = LED - 5mm [color="Green (560nm)" package="5 mm [THT]"]
  R44 = Resistor [tolerance=±5% resistance=330 package="0603 [SMD]"]
  R45 = Resistor [tolerance=±5% resistance=10k package="0603 [SMD]"]
  S33 = Pushbutton [package="[THT]"]
  R46 = Resistor [tolerance=±5% resistance=10k package="0603 [SMD]"]
  S34 = Pushbutton [package="[THT]"]
  R47 = Resistor [tolerance=±5% resistance=10k package="0603 [SMD]"]
  S35 = Pushbutton [package="[THT]"]
  R48 = Resistor [tolerance=±5% resistance=10k package="0603 [SMD]"]
  S36 = Pushbutton [package="[THT]"]
  LED53 = LED - 5mm [color="Green (560nm)" package="5 mm [THT]"]
  R49 = Resistor [tolerance=±5% resistance=330 package="0603 [SMD]"]
  J1 = Piezo Speaker
  DI1 = 16-segment display [package=THT]  # not connected
  DI2 = 16-segment display [package=THT]  # not connected
  LED54 = RGB LED (com. cathode, rgb) [package="5 mm [THT]"]
  R50 = Resistor [tolerance=±5% resistance=220 package=THT]
  R51 = Resistor [tolerance=±5% resistance=220 package=THT]
  R52 = Resistor [tolerance=±5% resistance=220 package=THT]
  LED55 = RGB LED (com. cathode, rgb) [package="5 mm [THT]"]
  R53 = Resistor [tolerance=±5% resistance=220 package=THT]
  R54 = Resistor [tolerance=±5% resistance=220 package=THT]
  R55 = Resistor [tolerance=±5% resistance=220 package=THT]
  R56 = Resistor [tolerance=±5% resistance=10k package="0603 [SMD]"]
  S37 = Pushbutton [package="[THT]"]
  R57 = Trimmer Potentiometer [maximum_resistance=10kΩ package=THT]
  LED56 = LED - 5mm [color="Yellow (585nm)" package="5 mm [THT]"]
  R58 = Resistor [tolerance=±5% resistance=220 package="0603 [SMD]"]
  R59 = Resistor [tolerance=±5% resistance=10k package="0603 [SMD]"]
  S38 = Pushbutton [package="[THT]"]
  LED57 = LED - 5mm [color="Green (560nm)" package="5 mm [THT]"]
  R60 = Resistor [tolerance=±5% resistance=330 package="0603 [SMD]"]
  LED58 = LED - 5mm [color="Green (560nm)" package="5 mm [THT]"]
  R61 = Resistor [tolerance=±5% resistance=330 package="0603 [SMD]"]
  R62 = Resistor [tolerance=±5% resistance=10k package="0603 [SMD]"]
  R63 = Resistor [tolerance=±5% resistance=10k package="0603 [SMD]"]
  R64 = Resistor [tolerance=±5% resistance=10k package="0603 [SMD]"]
  S39 = Pushbutton [package="[THT]"]
  S40 = Pushbutton [package="[THT]"]
  S41 = Pushbutton [package="[THT]"]
  LED59 = LED - 5mm [color="Yellow (585nm)" package="5 mm [THT]"]
  R65 = Resistor [tolerance=±5% resistance=220 package="0603 [SMD]"]
  U1 = MAX7219 [package=dil24]  # not connected
  U2 = MAX7219 [package=dil24]
  LED60 = LED - 5mm [color="Green (560nm)" package="5 mm [THT]"]
  R66 = Resistor [tolerance=±5% resistance=330 package="0603 [SMD]"]

nets:
  VSS: LCD4.VSS, LCM1602_IIC2.VSS
  VDD: LCD4.VDD, LCM1602_IIC2.VDD
  N1: LCD4.V0, LCM1602_IIC2.V0
  N2: LCD4.RS, LCM1602_IIC2.RS
  N3: LCD4.R/W, LCM1602_IIC2.RW
  N4: LCD4.E, LCM1602_IIC2.E
  N5: LCD4.DB0, LCM1602_IIC2.D0
  N6: LCD4.DB1, LCM1602_IIC2.D1
  N7: LCD4.DB2, LCM1602_IIC2.D2
  N8: LCD4.DB3, LCM1602_IIC2.D3
  N9: LCD4.DB4, LCM1602_IIC2.D4
  N10: LCD4.DB5, LCM1602_IIC2.D5
  N11: LCD4.DB6, LCM1602_IIC2.D6
  N12: LCD4.DB7, LCM1602_IIC2.D7
  N13: LCD4.LED-, LCM1602_IIC2.A
  N14: LCD4.LED+, LCM1602_IIC2.K
  N15: LCM1602_IIC2.GND, R22.Pin_0, R23.Pin_0, R24.Pin_0, R25.Pin_0, R26.Pin_0, R27.Pin_0
  N16: LCM1602_IIC2.VCC, S15.Pin_3, S15.Pin_4, S16.Pin_3, S16.Pin_4, S17.Pin_3, S17.Pin_4, S18.Pin_3, S18.Pin_4, S19.Pin_3, S19.Pin_4, S20.Pin_3, S20.Pin_4
  N17: LCM1602_IIC2.SDA, Part9.D20/SDA
  N18: LCM1602_IIC2.SCL, Part9.D21/SCL
  N19: Part8.VCC, J1.pin1
  N20: Part8.DIO, Part9.D15/RX3
  N21: Part8.CLK, Part9.D14/TX3
  N22: LCD5.V0, R57.wiper
  N23: LCD5.RS, Part9.D39
  N24: LCD5.DB4, Part9.D40
  N25: LCD5.DB5, Part9.D41
  N26: LCD5.DB6, Part9.D42
  N27: LCD5.DB7, Part9.D43
  N28: LCD5.LED+, S37.Pin_3, S37.Pin_4
  N29: LCD5.LED-, R56.Pin_0
  N30: LED31.cathode, R17.Pin_0
  N31: LED31.anode, Part9.D45
  N32: LED32.cathode, R13.Pin_0
  N33: LED32.anode, Part9.D48
  N34: LED33.cathode, R15.Pin_0
  N35: LED33.anode, Part9.D47
  N36: LED34.cathode, R16.Pin_0
  N37: LED34.anode, Part9.D46
  N38: LED35.cathode, R1.Pin_0
  N39: LED36.cathode, R2.Pin_0
  N40: LED37.cathode, R3.Pin_0
  N41: LED38.cathode, R4.Pin_0
  N42: LED39.cathode, R5.Pin_0
  N43: LED40.cathode, R6.Pin_0
  N44: LED41.cathode, R12.Pin_0
  N45: LED42.cathode, R11.Pin_0
  N46: LED43.cathode, R10.Pin_0
  N47: LED44.cathode, R9.Pin_0
  N48: LED45.cathode, R8.Pin_0
  N49: LED46.cathode, R7.Pin_0
  N50: Part9.A8, R45.Pin_1, S33.Pin_1, S33.Pin_2
  N51: Part9.A10, S18.Pin_1, S18.Pin_2, R25.Pin_1
  N52: Part9.A11, S19.Pin_1, S19.Pin_2, R26.Pin_1
  N53: Part9.A12, S20.Pin_1, S20.Pin_2, R27.Pin_1
  N54: Part9.A13, S17.Pin_1, S17.Pin_2, R24.Pin_1
  N55: Part9.A14, S16.Pin_1, S16.Pin_2, R23.Pin_1
  N56: Part9.A15, R22.Pin_1, S15.Pin_1, S15.Pin_2
  N57: Part9.A1, S11.Pin_1, S11.Pin_2, R21.Pin_1
  N58: Part9.A2, S12.Pin_1, S12.Pin_2, R19.Pin_1
  N59: Part9.A3, S13.Pin_1, S13.Pin_2, R18.Pin_1
  N60: Part9.A4, S14.Pin_1, S14.Pin_2, R20.Pin_1
  N61: Part9.A5, R46.Pin_1, S34.Pin_1, S34.Pin_2
  N62: Part9.A6, R47.Pin_1, S35.Pin_1, S35.Pin_2
  N63: Part9.A7, R48.Pin_1, S36.Pin_1, S36.Pin_2
  N64: Part9.D13_PWM, R52.Pin_1
  N65: Part9.D12_PWM, U2.CLK
  N66: Part9.D11_PWM, R50.Pin_1
  N67: Part9.D10_PWM, U2.LOAD
  N68: Part9.D9_PWM, U2.DIN
  N69: Part9.D2_PWM, J1.pin2
  N70: Part9.D4_PWM, R53.Pin_1
  N71: Part9.D5_PWM, R54.Pin_1
  N72: Part9.D6_PWM, R55.Pin_1
  N73: Part9.D7_PWM, R51.Pin_1
  N74: Part9.D22, LED60.anode
  N75: Part9.D23, R56.Pin_1, S37.Pin_1, S37.Pin_2
  N76: Part9.D24, R62.Pin_1, S39.Pin_1, S39.Pin_2
  N77: Part9.D25, R63.Pin_1, S40.Pin_1, S40.Pin_2
  N78: Part9.D26, R64.Pin_1, S41.Pin_1, S41.Pin_2
  N79: Part9.D27, LED58.anode
  N80: Part9.D29, LED59.anode
  N81: Part9.D30, R59.Pin_1, S38.Pin_1, S38.Pin_2
  N82: Part9.D31, LED56.anode
  N83: Part9.D32, LED57.anode
  N84: Part9.D34, LED48.anode
  N85: Part9.D35, LED49.anode
  N86: Part9.D36, LED50.anode
  N87: Part9.D44, LED53.anode
  N88: Part9.D49, LED47.anode
  N89: Part9.D53, LED51.anode
  N90: R1.Pin_1, R2.Pin_1, R3.Pin_1, R4.Pin_1, R5.Pin_1, R6.Pin_1, R7.Pin_1, R8.Pin_1, R9.Pin_1, R10.Pin_1, R11.Pin_1, R12.Pin_1
  N91: LED47.cathode, R14.Pin_0
  N92: R13.Pin_1, R14.Pin_1, R15.Pin_1, R16.Pin_1, R17.Pin_1
  N93: S11.Pin_3, S11.Pin_4, S12.Pin_3, S12.Pin_4, S13.Pin_3, S13.Pin_4, S14.Pin_3, S14.Pin_4
  N94: R18.Pin_0, R19.Pin_0, R20.Pin_0, R21.Pin_0
  N95: LED48.cathode, R28.Pin_0
  N96: LED49.cathode, R29.Pin_0
  N97: LED50.cathode, R30.Pin_0
  N98: R28.Pin_1, R29.Pin_1, R30.Pin_1, R31.Pin_1
  N99: R31.Pin_0, LED51.cathode
  N100: S21.Pin_1, S21.Pin_2, R33.Pin_1
  N101: S21.Pin_3, S21.Pin_4, S22.Pin_3, S22.Pin_4
  N102: S22.Pin_1, S22.Pin_2, R32.Pin_1
  N103: R32.Pin_0, R33.Pin_0
  N104: S23.Pin_1, S23.Pin_2, R34.Pin_1
  N105: S23.Pin_3, S23.Pin_4, S24.Pin_3, S24.Pin_4, S25.Pin_3, S25.Pin_4, S26.Pin_3, S26.Pin_4, S27.Pin_3, S27.Pin_4, S28.Pin_3, S28.Pin_4, S29.Pin_3, S29.Pin_4, S30.Pin_3, S30.Pin_4, S31.Pin_3, S31.Pin_4, S32.Pin_3, S32.Pin_4
  N106: S24.Pin_1, S24.Pin_2, R35.Pin_1
  N107: S25.Pin_1, S25.Pin_2, R36.Pin_1
  N108: S26.Pin_1, S26.Pin_2, R37.Pin_1
  N109: S27.Pin_1, S27.Pin_2, R38.Pin_1
  N110: S28.Pin_1, S28.Pin_2, R41.Pin_1
  N111: S29.Pin_1, S29.Pin_2, R42.Pin_1
  N112: S30.Pin_1, S30.Pin_2, R43.Pin_1
  N113: S31.Pin_1, S31.Pin_2, R40.Pin_1
  N114: S32.Pin_1, S32.Pin_2, R39.Pin_1
  N115: R34.Pin_0, R35.Pin_0, R36.Pin_0, R37.Pin_0, R38.Pin_0, R39.Pin_0, R40.Pin_0, R41.Pin_0, R42.Pin_0, R43.Pin_0
  N116: LED52.cathode, R44.Pin_0
  N117: R45.Pin_0, R46.Pin_0, R47.Pin_0, R48.Pin_0
  N118: S33.Pin_3, S33.Pin_4, S34.Pin_3, S34.Pin_4, S35.Pin_3, S35.Pin_4, S36.Pin_3, S36.Pin_4
  N119: LED53.cathode, R49.Pin_0
  N120: LED54.red_anode, R52.Pin_0
  N121: LED54.common_cathode, LED55.common_cathode, R57.leg2, R66.Pin_1
  N122: LED54.green_anode, R51.Pin_0
  N123: LED54.blue_anode, R50.Pin_0
  N124: LED55.red_anode, R55.Pin_0
  N125: LED55.green_anode, R54.Pin_0
  N126: LED55.blue_anode, R53.Pin_0
  N127: LED56.cathode, R58.Pin_0
  N128: S38.Pin_3, S38.Pin_4
  N129: LED57.cathode, R60.Pin_0
  N130: LED58.cathode, R61.Pin_0
  N131: R61.Pin_1, R65.Pin_1
  N132: R62.Pin_0, R63.Pin_0, R64.Pin_0
  N133: S39.Pin_3, S39.Pin_4, S40.Pin_3, S40.Pin_4, S41.Pin_3, S41.Pin_4
  N134: LED59.cathode, R65.Pin_0
  N135: LED60.cathode, R66.Pin_0

custom parts:
  LCD screen: A standard character display, usually with 2x16 characters. Comes in many colors.
  LCM1602 IIC: I2C-Module to use a 1602 or 2004 LCD on with the wire.h libory Serial LCD Modul
  TM1637: A 4 7-seg display
